# Fritzing sketch arduino gameχ (saved by Fritzing 0.9.3b)
breadboards: 1

parts:
  パーツ1 = Arduino Uno (Rev3)
  抵抗 = Resistor [tolerance=±5% resistance=330 package=THT]
  LED1 = LED - 5mm [color="Orange (605nm)" package="5 mm [THT]"]
  Orange_button = Pushbutton [package="[THT]"]
  抵抗_2 = Resistor [tolerance=±5% resistance=330 package=THT]
  LED2 = LED - 5mm [color="Green (555nm)" package="5 mm [THT]"]
  抵抗_3 = Resistor [tolerance=±5% resistance=330 package=THT]
  Green_button = Pushbutton [package="[THT]"]
  Red_button = Pushbutton [package="[THT]"]
  LED3 = LED - 5mm [color="Red (633nm)" package="5 mm [THT]"]
  Blue_button = Pushbutton [package="[THT]"]
  LED4 = LED - 5mm [color="Blue (430nm)" package="5 mm [THT]"]
  Reset_button = Pushbutton [package="[THT]"]
  抵抗_4 = Resistor [tolerance=±5% resistance=330 package=THT]
  抵抗_5 = Resistor [tolerance=±5% resistance=330 package=THT]
  抵抗_6 = Resistor [tolerance=±5% resistance=330 package=THT]
  抵抗_7 = Resistor [tolerance=±5% resistance=330 package=THT]
  抵抗_8 = Resistor [tolerance=±5% resistance=330 package=THT]
  抵抗_9 = Resistor [tolerance=±5% resistance=330 package=THT]

nets:
  N1: パーツ1.D8, Red_button.Pin_3, Red_button.Pin_4, 抵抗_5.Pin_0
  N2: パーツ1.D9_PWM, Blue_button.Pin_3, Blue_button.Pin_4, 抵抗_4.Pin_0
  N3: パーツ1.D10_PWM/SS, Green_button.Pin_3, Green_button.Pin_4, 抵抗_9.Pin_0
  N4: パーツ1.D11_PWM/MOSI, Orange_button.Pin_3, Orange_button.Pin_4, 抵抗_2.Pin_0
  N5: パーツ1.D12/MISO, Reset_button.Pin_3, Reset_button.Pin_4, 抵抗_6.Pin_0
  N6: パーツ1.GND, 抵抗.Pin_1, 抵抗_2.Pin_1, 抵抗_3.Pin_1, 抵抗_4.Pin_1, 抵抗_5.Pin_1, 抵抗_6.Pin_1, 抵抗_7.Pin_1, 抵抗_8.Pin_1, 抵抗_9.Pin_1
  N7: パーツ1.D2, LED3.anode
  N8: パーツ1.D3_PWM, LED4.anode
  N9: パーツ1.D4, LED2.anode
  N10: パーツ1.D5_PWM, LED1.anode
  N11: パーツ1.5V, Orange_button.Pin_1, Orange_button.Pin_2, Green_button.Pin_1, Green_button.Pin_2, Red_button.Pin_1, Red_button.Pin_2, Blue_button.Pin_1, Blue_button.Pin_2, Reset_button.Pin_1, Reset_button.Pin_2
  N12: 抵抗.Pin_0, LED1.cathode
  N13: LED2.cathode, 抵抗_3.Pin_0
  N14: LED3.cathode, 抵抗_8.Pin_0
  N15: LED4.cathode, 抵抗_7.Pin_0
